// Logisim project main.circ as structural Verilog: 17 circuits, main circuit main
module main (
);

  wire and_1_out, bulletcontroller_1_defeattartget, bulletcontroller_2_defeattartget, clock, curClock,
       d_ff_1_q, difPlayer, drBulletE, drBulletP, drivecontroller_1_isdrive, drPlayer, resetButton,
       resetOutput, shotPlayer, winEnemy, winPlayer;
  wire [1:0] drivecontroller_1_way, wayCur;
  wire [4:0] display_printer_1_column, rq1, rq2, rq3, xbe, xbp, xOutput, xpCur, ypCur;
  wire [6:0] keyboardData;
  wire [30:0] dispaystategame_1_out_5, dispaystategame_1_out_6, dispaystategame_1_out_7,
       dispaystategame_1_out_8, dispaystategame_1_out_9, dispaystategame_1_out_10, dispaystategame_1_out_11;
  wire [31:0] a1, a2, a3, cr, dispalycontroller_1_out_8, dispalycontroller_1_out_9,
       dispalycontroller_1_out_10, dispalycontroller_1_out_11, dispalycontroller_1_out_12,
       dispalycontroller_1_out_13, dispalycontroller_1_out_14, dispalycontroller_1_out_15,
       dispalycontroller_1_out_16, dispalycontroller_1_out_17, dispalycontroller_1_out_18,
       dispalycontroller_1_out_19, dispalycontroller_1_out_20, dispalycontroller_1_out_21,
       dispalycontroller_1_out_22, dispalycontroller_1_out_23, dispalycontroller_1_out_24,
       dispalycontroller_1_out_25, dispalycontroller_1_out_26, dispalycontroller_1_out_27,
       dispalycontroller_1_out_28, dispalycontroller_1_out_29, dispalycontroller_1_out_30,
       dispalycontroller_1_out_31, dispalycontroller_1_out_32, dispalycontroller_1_out_33,
       dispalycontroller_1_out_34, dispalycontroller_1_out_35, dispalycontroller_1_out_36,
       dispalycontroller_1_out_37, dispalycontroller_1_out_38, dispalycontroller_1_out_39,
       display_printer_1_picture, lbe, lbp, lp1, lp2, lp3;

  Pull_Resistor pull_resistor_1 (.node(clock));
  assign clock = and_1_out ? curClock : 1'bz;  // Controlled_Buffer controlled_buffer_1
  and and_1 (and_1_out, ~winPlayer, d_ff_1_q, ~winEnemy);  // AND_Gate
  Clock clock_1 (.out(curClock));
  D_Flip_Flop d_ff_1 (.clk(resetButton), .D(resetButton), .Q(d_ff_1_q));  // open: Qn, preset, en, reset
  bulletController bulletcontroller_1 (
    .xStart(5'b11101), .yStart(5'b11101), .way(2'b00), .shot(clock), .reset(resetOutput),
    .stateUpdate(drBulletE), .clock(drBulletE), .xEnemy(xpCur), .yEnemy(ypCur), .outputLine(lbe),
    .xOutput(xbe), .defeatTartget(bulletcontroller_1_defeattartget));
  D_Flip_Flop d_ff_2 (
    .clk(bulletcontroller_1_defeattartget), .D(bulletcontroller_1_defeattartget), .Q(winEnemy),
    .reset(resetButton));  // open: Qn, preset, en
  DotMatrix #(.inputtype("row"), .matrixcols(31)) dotmatrix_1 (
    .row0(dispaystategame_1_out_5), .row1(dispaystategame_1_out_6), .row2(dispaystategame_1_out_7),
    .row3(dispaystategame_1_out_8), .row4(dispaystategame_1_out_9), .row5(dispaystategame_1_out_10),
    .row6(dispaystategame_1_out_11));
  dispayStateGame dispaystategame_1 (
    .clock(curClock), .wEnemy(winEnemy), .wPlayer(winPlayer), .out_5(dispaystategame_1_out_5),
    .out_6(dispaystategame_1_out_6), .out_7(dispaystategame_1_out_7), .out_8(dispaystategame_1_out_8),
    .out_9(dispaystategame_1_out_9), .out_10(dispaystategame_1_out_10), .out_11(dispaystategame_1_out_11),
    .start(resetButton));
  DotMatrix #(.matrixcols(32), .matrixrows(32)) dotmatrix_2 (
    .col0(dispalycontroller_1_out_8), .col1(dispalycontroller_1_out_9), .col2(dispalycontroller_1_out_10),
    .col3(dispalycontroller_1_out_11), .col4(dispalycontroller_1_out_12), .col5(dispalycontroller_1_out_13),
    .col6(dispalycontroller_1_out_14), .col7(dispalycontroller_1_out_15), .col8(dispalycontroller_1_out_16),
    .col9(dispalycontroller_1_out_17), .col10(dispalycontroller_1_out_18),
    .col11(dispalycontroller_1_out_19), .col12(dispalycontroller_1_out_20),
    .col13(dispalycontroller_1_out_21), .col14(dispalycontroller_1_out_22),
    .col15(dispalycontroller_1_out_23), .col16(dispalycontroller_1_out_24),
    .col17(dispalycontroller_1_out_25), .col18(dispalycontroller_1_out_26),
    .col19(dispalycontroller_1_out_27), .col20(dispalycontroller_1_out_28),
    .col21(dispalycontroller_1_out_29), .col22(dispalycontroller_1_out_30),
    .col23(dispalycontroller_1_out_31), .col24(dispalycontroller_1_out_32),
    .col25(dispalycontroller_1_out_33), .col26(dispalycontroller_1_out_34),
    .col27(dispalycontroller_1_out_35), .col28(dispalycontroller_1_out_36),
    .col29(dispalycontroller_1_out_37), .col30(dispalycontroller_1_out_38), .col31(dispalycontroller_1_out_39));
  dispalyController dispalycontroller_1 (
    .clock(clock), .column(display_printer_1_column), .picture(display_printer_1_picture),
    .out_8(dispalycontroller_1_out_8), .out_20(dispalycontroller_1_out_20),
    .out_32(dispalycontroller_1_out_32), .out_9(dispalycontroller_1_out_9),
    .out_21(dispalycontroller_1_out_21), .out_33(dispalycontroller_1_out_33),
    .out_10(dispalycontroller_1_out_10), .out_22(dispalycontroller_1_out_22),
    .out_34(dispalycontroller_1_out_34), .out_11(dispalycontroller_1_out_11),
    .out_23(dispalycontroller_1_out_23), .out_35(dispalycontroller_1_out_35),
    .out_12(dispalycontroller_1_out_12), .out_24(dispalycontroller_1_out_24),
    .out_36(dispalycontroller_1_out_36), .out_13(dispalycontroller_1_out_13),
    .out_25(dispalycontroller_1_out_25), .out_37(dispalycontroller_1_out_37),
    .out_14(dispalycontroller_1_out_14), .out_26(dispalycontroller_1_out_26),
    .out_38(dispalycontroller_1_out_38), .out_15(dispalycontroller_1_out_15),
    .out_27(dispalycontroller_1_out_27), .out_39(dispalycontroller_1_out_39),
    .out_16(dispalycontroller_1_out_16), .out_28(dispalycontroller_1_out_28),
    .out_17(dispalycontroller_1_out_17), .out_29(dispalycontroller_1_out_29),
    .out_18(dispalycontroller_1_out_18), .out_30(dispalycontroller_1_out_30),
    .out_19(dispalycontroller_1_out_19), .out_31(dispalycontroller_1_out_31), .selectCol1(a1),
    .selectCol2(a2), .selectCol3(a3), .getRow1(rq1), .getRow2(rq2), .getRow3(rq3), .currentCol(cr),
    .getCurr(display_printer_1_column));
  Button reset (.out(resetButton));
  Keyboard #(.buflen(2), .trigger("falling")) keyboard_1 (.clk(clock), .data(keyboardData));  // open: re, clr, avail
  bulletController bulletcontroller_2 (
    .xStart(xpCur), .yStart(ypCur), .way(wayCur), .shot(shotPlayer), .reset(resetOutput),
    .stateUpdate(drBulletP), .clock(drBulletP), .xEnemy(5'b11101), .yEnemy(5'b11101), .outputLine(lbp),
    .xOutput(xbp), .defeatTartget(bulletcontroller_2_defeattartget));
  D_Flip_Flop d_ff_3 (
    .clk(bulletcontroller_2_defeattartget), .D(bulletcontroller_2_defeattartget), .Q(winPlayer),
    .reset(resetButton));  // open: Qn, preset, en
  driveController drivecontroller_1 (
    .input_char(keyboardData), .way(drivecontroller_1_way), .isDrive(drivecontroller_1_isdrive),
    .isShot(shotPlayer));
  display_printer display_printer_1 (
    .clock(clock), .x_player(xOutput), .x_bullet_player(xbp), .x_enemy({5{1'b0}}), .x_bullet_enemy(xbe),
    .draw_player(drPlayer), .draw_bullet_player(drBulletP), .draw_bullet_enemy(drBulletE),
    .player_line_1(lp1), .player_line_2(lp2), .player_line_3(lp3), .picture(display_printer_1_picture),
    .player_bullet_line(lbp), .enemy_line_1({32{1'b0}}), .enemy_line_2({32{1'b0}}),
    .enemy_line_3({32{1'b0}}), .column(display_printer_1_column), .enemy_bullet_line(lbe), .current_line(cr),
    .reset(resetButton), .output_reset(resetOutput), .differentPlayer(difPlayer));  // open: draw_enemy
  tankObjectPlayer tankobjectplayer_1 (
    .clock(clock), .isDrive(drivecontroller_1_isdrive), .Reset(resetOutput), .way(drivecontroller_1_way),
    .X_output(xOutput), .out_12(lp1), .out_13(lp2), .out_15(lp3), .stateUpdate(drPlayer), .input_line_1(a1),
    .input_line_2(a2), .input_line_3(a3), .req_line_1(rq1), .req_line_2(rq2), .req_line_3(rq3),
    .differentCord(difPlayer), .xCur(xpCur), .yCur(ypCur), .wayCur(wayCur));

  // Notes on the sheet:
  //   RESET
  //   BULLET ENEMY
  //   временное решение
  //   временное решение
  //   BULLET PLAYER
  //   DISPLAY CONTROL
  //   TANK PLAYER
endmodule

module dispalyController (
  input  clock,
  input  [4:0] column,
  input  [31:0] picture,
  input  [4:0] getRow1,
  input  [4:0] getRow3,
  input  [4:0] getRow2,
  input  [4:0] getCurr,
  output [31:0] out_8,
  output [31:0] out_9,
  output [31:0] out_10,
  output [31:0] out_11,
  output [31:0] out_12,
  output [31:0] out_13,
  output [31:0] out_14,
  output [31:0] out_15,
  output [31:0] out_16,
  output [31:0] out_17,
  output [31:0] out_18,
  output [31:0] out_19,
  output [31:0] out_20,
  output [31:0] out_21,
  output [31:0] out_22,
  output [31:0] out_23,
  output [31:0] out_24,
  output [31:0] out_25,
  output [31:0] out_26,
  output [31:0] out_27,
  output [31:0] out_28,
  output [31:0] out_29,
  output [31:0] out_30,
  output [31:0] out_31,
  output [31:0] out_32,
  output [31:0] out_33,
  output [31:0] out_34,
  output [31:0] out_35,
  output [31:0] out_36,
  output [31:0] out_37,
  output [31:0] out_38,
  output [31:0] out_39,
  output [31:0] selectCol1,
  output [31:0] selectCol3,
  output [31:0] selectCol2,
  output [31:0] currentCol
);

  wire c0, c1, c2, c3, c4, c5, c6, c7, c8, c9, c10, c11, c12, c13, c14, c15, c16, c17, c18, c19, c20, c21,
       c22, c23, c24, c25, c26, c27, c28, c29, c30, c31;
  wire [31:0] s0, s1, s2, s3, s4, s5, s6, s7, s8, s9, s10, s11, s12, s13, s14, s15, s16, s17, s18, s19, s20,
       s21, s22, s23, s24, s25, s26, s27, s28, s29, s30, s31;

  Register #(.width(32), .trigger("falling")) register_1 (.D(s0), .en(c0), .Q(out_8), .clk(clock));  // open: clr
  Register #(.width(32), .trigger("falling")) register_2 (.D(s12), .en(c12), .Q(out_20), .clk(clock));  // open: clr
  Register #(.width(32), .trigger("falling")) register_3 (.D(s24), .en(c24), .Q(out_32), .clk(clock));  // open: clr
  Register #(.width(32), .trigger("falling")) register_4 (.D(s1), .en(c1), .Q(out_9), .clk(clock));  // open: clr
  Register #(.width(32), .trigger("falling")) register_5 (.D(s13), .en(c13), .Q(out_21), .clk(clock));  // open: clr
  Register #(.width(32), .trigger("falling")) register_6 (.D(s25), .en(c25), .Q(out_33), .clk(clock));  // open: clr
  Register #(.width(32), .trigger("falling")) register_7 (.D(s2), .en(c2), .Q(out_10), .clk(clock));  // open: clr
  Register #(.width(32), .trigger("falling")) register_8 (.D(s14), .en(c14), .Q(out_22), .clk(clock));  // open: clr
  Register #(.width(32), .trigger("falling")) register_9 (.D(s26), .en(c26), .Q(out_34), .clk(clock));  // open: clr
  Demultiplexer #(.select(5), .width(32), .enable("false")) demultiplexer_1 (
    .out0(s0), .out1(s1), .out2(s2), .out3(s3), .out4(s4), .out5(s5), .out6(s6), .out7(s7), .out8(s8),
    .out9(s9), .out10(s10), .out11(s11), .out12(s12), .out13(s13), .out14(s14), .out15(s15), .out16(s16),
    .out17(s17), .out18(s18), .out19(s19), .out20(s20), .out21(s21), .out22(s22), .out23(s23), .out24(s24),
    .out25(s25), .out26(s26), .out27(s27), .out28(s28), .out29(s29), .out30(s30), .out31(s31), .in(picture),
    .sel(column));
  Register #(.width(32), .trigger("falling")) register_10 (.D(s3), .en(c3), .Q(out_11), .clk(clock));  // open: clr
  Register #(.width(32), .trigger("falling")) register_11 (.D(s15), .en(c15), .Q(out_23), .clk(clock));  // open: clr
  Register #(.width(32), .trigger("falling")) register_12 (.D(s27), .en(c27), .Q(out_35), .clk(clock));  // open: clr
  Register #(.width(32), .trigger("falling")) register_13 (.D(s4), .en(c4), .Q(out_12), .clk(clock));  // open: clr
  Register #(.width(32), .trigger("falling")) register_14 (.D(s16), .en(c16), .Q(out_24), .clk(clock));  // open: clr
  Register #(.width(32), .trigger("falling")) register_15 (.D(s28), .en(c28), .Q(out_36), .clk(clock));  // open: clr
  Multiplexer #(.select(5), .width(32), .enable("false")) multiplexer_1 (
    .in0(out_8), .in1(out_9), .in2(out_10), .in3(out_11), .in4(out_12), .in5(out_13), .in6(out_14),
    .in7(out_15), .in8(out_16), .in9(out_17), .in10(out_18), .in11(out_19), .in12(out_20), .in13(out_21),
    .in14(out_22), .in15(out_23), .in16(out_24), .in17(out_25), .in18(out_26), .in19(out_27), .in20(out_28),
    .in21(out_29), .in22(out_30), .in23(out_31), .in24(out_32), .in25(out_33), .in26(out_34), .in27(out_35),
    .in28(out_36), .in29(out_37), .in30(out_38), .in31(out_39), .out(selectCol1), .sel(getRow1));
  Multiplexer #(.select(5), .width(32), .enable("false")) multiplexer_2 (
    .in0(out_8), .in1(out_9), .in2(out_10), .in3(out_11), .in4(out_12), .in5(out_13), .in6(out_14),
    .in7(out_15), .in8(out_16), .in9(out_17), .in10(out_18), .in11(out_19), .in12(out_20), .in13(out_21),
    .in14(out_22), .in15(out_23), .in16(out_24), .in17(out_25), .in18(out_26), .in19(out_27), .in20(out_28),
    .in21(out_29), .in22(out_30), .in23(out_31), .in24(out_32), .in25(out_33), .in26(out_34), .in27(out_35),
    .in28(out_36), .in29(out_37), .in30(out_38), .in31(out_39), .out(selectCol2), .sel(getRow2));
  Register #(.width(32), .trigger("falling")) register_16 (.D(s5), .en(c5), .Q(out_13), .clk(clock));  // open: clr
  Register #(.width(32), .trigger("falling")) register_17 (.D(s17), .en(c17), .Q(out_25), .clk(clock));  // open: clr
  Register #(.width(32), .trigger("falling")) register_18 (.D(s29), .en(c29), .Q(out_37), .clk(clock));  // open: clr
  Register #(.width(32), .trigger("falling")) register_19 (.D(s6), .en(c6), .Q(out_14), .clk(clock));  // open: clr
  Register #(.width(32), .trigger("falling")) register_20 (.D(s18), .en(c18), .Q(out_26), .clk(clock));  // open: clr
  Register #(.width(32), .trigger("falling")) register_21 (.D(s30), .en(c30), .Q(out_38), .clk(clock));  // open: clr
  Register #(.width(32), .trigger("falling")) register_22 (.D(s7), .en(c7), .Q(out_15), .clk(clock));  // open: clr
  Register #(.width(32), .trigger("falling")) register_23 (.D(s19), .en(c19), .Q(out_27), .clk(clock));  // open: clr
  Register #(.width(32), .trigger("falling")) register_24 (.D(s31), .en(c31), .Q(out_39), .clk(clock));  // open: clr
  Register #(.width(32), .trigger("falling")) register_25 (.D(s8), .en(c8), .Q(out_16), .clk(clock));  // open: clr
  Register #(.width(32), .trigger("falling")) register_26 (.D(s20), .en(c20), .Q(out_28), .clk(clock));  // open: clr
  Demultiplexer #(.select(5), .enable("false")) demultiplexer_2 (
    .out0(c0), .out1(c1), .out2(c2), .out3(c3), .out4(c4), .out5(c5), .out6(c6), .out7(c7), .out8(c8),
    .out9(c9), .out10(c10), .out11(c11), .out12(c12), .out13(c13), .out14(c14), .out15(c15), .out16(c16),
    .out17(c17), .out18(c18), .out19(c19), .out20(c20), .out21(c21), .out22(c22), .out23(c23), .out24(c24),
    .out25(c25), .out26(c26), .out27(c27), .out28(c28), .out29(c29), .out30(c30), .out31(c31), .in(1'b1),
    .sel(column));
  Register #(.width(32), .trigger("falling")) register_27 (.D(s9), .en(c9), .Q(out_17), .clk(clock));  // open: clr
  Register #(.width(32), .trigger("falling")) register_28 (.D(s21), .en(c21), .Q(out_29), .clk(clock));  // open: clr
  Register #(.width(32), .trigger("falling")) register_29 (.D(s10), .en(c10), .Q(out_18), .clk(clock));  // open: clr
  Register #(.width(32), .trigger("falling")) register_30 (.D(s22), .en(c22), .Q(out_30), .clk(clock));  // open: clr
  Register #(.width(32), .trigger("falling")) register_31 (.D(s11), .en(c11), .Q(out_19), .clk(clock));  // open: clr
  Register #(.width(32), .trigger("falling")) register_32 (.D(s23), .en(c23), .Q(out_31), .clk(clock));  // open: clr
  Multiplexer #(.select(5), .width(32), .enable("false")) multiplexer_3 (
    .in0(out_8), .in1(out_9), .in2(out_10), .in3(out_11), .in4(out_12), .in5(out_13), .in6(out_14),
    .in7(out_15), .in8(out_16), .in9(out_17), .in10(out_18), .in11(out_19), .in12(out_20), .in13(out_21),
    .in14(out_22), .in15(out_23), .in16(out_24), .in17(out_25), .in18(out_26), .in19(out_27), .in20(out_28),
    .in21(out_29), .in22(out_30), .in23(out_31), .in24(out_32), .in25(out_33), .in26(out_34), .in27(out_35),
    .in28(out_36), .in29(out_37), .in30(out_38), .in31(out_39), .out(selectCol3), .sel(getRow3));
  Multiplexer #(.select(5), .width(32), .enable("false")) multiplexer_4 (
    .in0(out_8), .in1(out_9), .in2(out_10), .in3(out_11), .in4(out_12), .in5(out_13), .in6(out_14),
    .in7(out_15), .in8(out_16), .in9(out_17), .in10(out_18), .in11(out_19), .in12(out_20), .in13(out_21),
    .in14(out_22), .in15(out_23), .in16(out_24), .in17(out_25), .in18(out_26), .in19(out_27), .in20(out_28),
    .in21(out_29), .in22(out_30), .in23(out_31), .in24(out_32), .in25(out_33), .in26(out_34), .in27(out_35),
    .in28(out_36), .in29(out_37), .in30(out_38), .in31(out_39), .out(currentCol), .sel(getCurr));

  // Other names for the same wires on the sheet: clk = clock; col[4:0] = column; curr[4:0] = getCurr;
  //   o0[31:0] = out_8; o1[31:0] = out_9; o2[31:0] = out_10; o3[31:0] = out_11; o4[31:0] = out_12; o5[31:0] = out_13;
  //   o6[31:0] = out_14; o7[31:0] = out_15; o8[31:0] = out_16; o9[31:0] = out_17; o10[31:0] = out_18;
  //   o11[31:0] = out_19; o12[31:0] = out_20; o13[31:0] = out_21; o14[31:0] = out_22; o15[31:0] = out_23;
  //   o16[31:0] = out_24; o17[31:0] = out_25; o18[31:0] = out_26; o19[31:0] = out_27; o20[31:0] = out_28;
  //   o21[31:0] = out_29; o22[31:0] = out_30; o23[31:0] = out_31; o24[31:0] = out_32; o25[31:0] = out_33;
  //   o26[31:0] = out_34; o27[31:0] = out_35; o28[31:0] = out_36; o29[31:0] = out_37; o30[31:0] = out_38;
  //   o31[31:0] = out_39; row1[4:0] = getRow1; row2[4:0] = getRow2; row3[4:0] = getRow3

  // Notes on the sheet:
  //   INPUT LINE
  //   INPUT COORDINATES
endmodule

module tankObjectPlayer (
  input  [31:0] input_line_1,
  input  [31:0] input_line_2,
  input  [31:0] input_line_3,
  input  clock,
  input  stateUpdate,
  input  isDrive,
  input  [1:0] way,
  input  Reset,
  output [4:0] req_line_1,
  output [4:0] req_line_2,
  output [4:0] req_line_3,
  output [31:0] out_12,
  output [31:0] out_13,
  output [4:0] X_output,
  output [31:0] out_15,
  output differentCord,
  output [4:0] xCur,
  output [4:0] yCur,
  output [1:0] wayCur
);

  wire comparator_1_gt, comparator_1_lt, comparator_2_gt, comparator_2_lt, comparator_3_gt, comparator_3_lt,
       comparator_4_gt, comparator_4_lt, comparator_5_gt, comparator_5_lt, drive, or_2_out, or_3_out,
       or_5_out, or_6_out, or_7_out;
  wire [1:0] DirectionTank_q, dirTank1, multiplexer_2_out;
  wire [4:0] multiplexer_3_out, multiplexer_5_out, rq1, rq1_2, x_cord_checker_1_x_cord_output,
       y_cord_checker_1_y_cord_output;
  wire [31:0] pctIn1, pctIn2, pctIn3;

  Multiplexer #(.width(5), .enable("false")) multiplexer_1 (.in0(rq1_2), .in1(rq1), .out(req_line_1), .sel(wayCur[0]));
  or or_1 (drive, isDrive, Reset);
  Comparator #(.width(5)) comparator_1 (
    .a(xCur), .b(X_output), .gt(comparator_1_gt), .lt(comparator_1_lt));  // open: eq
  Comparator #(.width(2)) comparator_2 (
    .a(dirTank1), .b(wayCur), .gt(comparator_2_gt), .lt(comparator_2_lt));  // open: eq
  Comparator #(.width(32)) comparator_3 (
    .a(pctIn1), .b(out_12), .gt(comparator_3_gt), .lt(comparator_3_lt));  // open: eq
  Comparator #(.width(32)) comparator_4 (
    .a(pctIn2), .b(out_13), .gt(comparator_4_gt), .lt(comparator_4_lt));  // open: eq
  Comparator #(.width(32)) comparator_5 (
    .a(pctIn3), .b(out_15), .gt(comparator_5_gt), .lt(comparator_5_lt));  // open: eq
  or or_2 (or_2_out, comparator_1_gt, comparator_1_lt);
  or or_3 (or_3_out, comparator_2_gt, comparator_2_lt);
  or or_4 (differentCord, or_2_out, or_3_out, or_5_out, or_6_out, or_7_out);
  or or_5 (or_5_out, comparator_3_gt, comparator_3_lt);
  or or_6 (or_6_out, comparator_4_gt, comparator_4_lt);
  or or_7 (or_7_out, comparator_5_gt, comparator_5_lt);
  Multiplexer #(.width(2), .enable("false")) multiplexer_2 (
    .in0(way), .in1(2'b01), .out(multiplexer_2_out), .sel(Reset));
  X_cord_checker x_cord_checker_1 (
    .Y_cord(yCur), .X_cord(xCur), .Way(wayCur), .req_1(rq1_2), .line_1(input_line_1),
    .X_cord_output(x_cord_checker_1_x_cord_output));
  Register #(.width(2), .trigger("falling")) DirectionTank (
    .D(multiplexer_2_out), .en(drive), .Q(DirectionTank_q), .clk(clock));  // open: clr
  Multiplexer #(.width(5), .enable("false")) multiplexer_3 (
    .in0(x_cord_checker_1_x_cord_output), .in1(5'b01111), .out(multiplexer_3_out), .sel(Reset));
  Multiplexer #(.width(2), .enable("false")) multiplexer_4 (
    .in0(DirectionTank_q), .in1(way), .out(wayCur), .sel(drive));
  Register #(.width(5), .trigger("falling")) xTank (
    .D(multiplexer_3_out), .en(drive), .Q(xCur), .clk(clock));  // open: clr
  Register #(.width(2), .trigger("falling")) DirectionTank1 (
    .D(wayCur), .Q(dirTank1), .clk(stateUpdate), .clr(Reset));  // open: en
  Register #(.width(5), .trigger("falling")) xTank1 (
    .D(xCur), .Q(X_output), .clk(stateUpdate), .clr(Reset));  // open: en
  Y_cord_checker y_cord_checker_1 (
    .Y_cord(yCur), .X_cord(xCur), .Way(wayCur), .req_1(rq1), .Y_cord_output(y_cord_checker_1_y_cord_output),
    .req_2(req_line_2), .req_3(req_line_3), .line_1(input_line_1), .line_2(input_line_2),
    .line_3(input_line_3));
  drawTank drawtank_1 (.Y(yCur), .Way(wayCur), .line_1(pctIn1), .line_2(pctIn2), .line_3(pctIn3));
  Multiplexer #(.width(5), .enable("false")) multiplexer_5 (
    .in0(y_cord_checker_1_y_cord_output), .in1(5'b00001), .out(multiplexer_5_out), .sel(Reset));
  Register #(.width(32), .trigger("falling")) register_1 (
    .D(pctIn1), .Q(out_12), .clk(stateUpdate), .clr(Reset));  // open: en
  Register #(.width(32), .trigger("falling")) register_2 (
    .D(pctIn2), .Q(out_13), .clk(stateUpdate), .clr(Reset));  // open: en
  Register #(.width(32), .trigger("falling")) register_3 (
    .D(pctIn3), .Q(out_15), .clk(stateUpdate), .clr(Reset));  // open: en
  Register #(.width(5), .trigger("falling")) yTank (
    .D(multiplexer_5_out), .en(drive), .Q(yCur), .clk(clock));  // open: clr

  // Other names for the same wires on the sheet: clk = clock; dirTank[1:0] = wayCur; pctOut1[31:0] = out_12;
  //   pctOut2[31:0] = out_13; pctOut3[31:0] = out_15; rq2[4:0] = req_line_2; rq3[4:0] = req_line_3;
  //   state_up = stateUpdate; x_cord_tank[4:0] = xCur; x_cord_tank1[4:0] = X_output; y_cord_tank[4:0] = yCur

  // Notes on the sheet:
  //   INPUTS
  //   IS DIFFERENT COORDINAT OR ROTATE TANK
  //   X COORDINATE TANK
  //   DIRECTION TANK
  //   LAST DIRECTION TANK
  //   LAST X COORDINATE TANK
  //   OUTPUTS
  //   Y COORDINATE TANK
  //   IMAGE TANK
endmodule

module drawTank (
  input  [4:0] Y,
  input  [1:0] Way,
  output [31:0] line_1,
  output [31:0] line_2,
  output [31:0] line_3
);

  wire [4:0] dec5_1_out, dec5_2_out, dec5_3_out, dec5_4_out, dec5_5_out, inc5_1_out, inc5_2_out, inc5_3_out,
       inc5_4_out, inc5_5_out;
  wire [31:0] down_Line_1, down_Line_2, down_Line_3, left_Line_1, left_Line_2, left_Line_3, shifter_2_out,
       shifter_3_out, shifter_4_out, shifter_5_out, shifter_6_out, shifter_7_out, shifter_8_out,
       shifter_9_out, shifter_10_out, shifter_11_out, shifter_12_out, shifter_13_out, shifter_14_out,
       shifter_15_out, shifter_16_out, shifter_17_out, shifter_18_out, up_Line_1, up_Line_2, up_Line_3;

  dec5 dec5_1 (.in(Y), .out(dec5_1_out));
  inc5 inc5_1 (.in(Y), .out(inc5_1_out));
  dec5 dec5_2 (.in(Y), .out(dec5_2_out));
  inc5 inc5_2 (.in(Y), .out(inc5_2_out));
  Shifter #(.width(32)) shifter_1 (.in(32'h1), .\dist (Y), .out(left_Line_1));
  Shifter #(.width(32)) shifter_2 (.in(32'h1), .\dist (dec5_1_out), .out(shifter_2_out));
  Shifter #(.width(32)) shifter_3 (.in(32'h1), .\dist (Y), .out(shifter_3_out));
  Shifter #(.width(32)) shifter_4 (.in(32'h1), .\dist (inc5_1_out), .out(shifter_4_out));
  Shifter #(.width(32)) shifter_5 (.in(32'h1), .\dist (dec5_2_out), .out(shifter_5_out));
  Shifter #(.width(32)) shifter_6 (.in(32'h1), .\dist (inc5_2_out), .out(shifter_6_out));
  assign left_Line_2 = shifter_2_out | shifter_3_out | shifter_4_out;  // OR_Gate or_1, 32 bits wide
  assign left_Line_3 = shifter_5_out | shifter_6_out;  // OR_Gate or_2, 32 bits wide
  dec5 dec5_3 (.in(Y), .out(dec5_3_out));
  inc5 inc5_3 (.in(Y), .out(inc5_3_out));
  dec5 dec5_4 (.in(Y), .out(dec5_4_out));
  Shifter #(.width(32)) shifter_7 (.in(32'h1), .\dist (dec5_3_out), .out(shifter_7_out));
  Shifter #(.width(32)) shifter_8 (.in(32'h1), .\dist (Y), .out(shifter_8_out));
  Shifter #(.width(32)) shifter_9 (.in(32'h1), .\dist (inc5_3_out), .out(shifter_9_out));
  Shifter #(.width(32)) shifter_10 (.in(32'h1), .\dist (Y), .out(shifter_10_out));
  Shifter #(.width(32)) shifter_11 (.in(32'h1), .\dist (dec5_4_out), .out(shifter_11_out));
  Shifter #(.width(32)) shifter_12 (.in(32'h1), .\dist (Y), .out(shifter_12_out));
  assign up_Line_1 = shifter_7_out | shifter_8_out;  // OR_Gate or_3, 32 bits wide
  assign up_Line_2 = shifter_9_out | shifter_10_out;  // OR_Gate or_4, 32 bits wide
  assign up_Line_3 = shifter_11_out | shifter_12_out;  // OR_Gate or_5, 32 bits wide
  inc5 inc5_4 (.in(Y), .out(inc5_4_out));
  dec5 dec5_5 (.in(Y), .out(dec5_5_out));
  inc5 inc5_5 (.in(Y), .out(inc5_5_out));
  Shifter #(.width(32)) shifter_13 (.in(32'h1), .\dist (inc5_4_out), .out(shifter_13_out));
  Shifter #(.width(32)) shifter_14 (.in(32'h1), .\dist (Y), .out(shifter_14_out));
  Shifter #(.width(32)) shifter_15 (.in(32'h1), .\dist (dec5_5_out), .out(shifter_15_out));
  Shifter #(.width(32)) shifter_16 (.in(32'h1), .\dist (Y), .out(shifter_16_out));
  Shifter #(.width(32)) shifter_17 (.in(32'h1), .\dist (inc5_5_out), .out(shifter_17_out));
  Shifter #(.width(32)) shifter_18 (.in(32'h1), .\dist (Y), .out(shifter_18_out));
  assign down_Line_1 = shifter_13_out | shifter_14_out;  // OR_Gate or_6, 32 bits wide
  assign down_Line_2 = shifter_15_out | shifter_16_out;  // OR_Gate or_7, 32 bits wide
  assign down_Line_3 = shifter_17_out | shifter_18_out;  // OR_Gate or_8, 32 bits wide
  Multiplexer #(.select(2), .width(32), .enable("false")) multiplexer_1 (
    .in0(left_Line_1), .in1(up_Line_1), .in2(left_Line_3), .in3(down_Line_1), .out(line_1), .sel(Way));
  Multiplexer #(.select(2), .width(32), .enable("false")) multiplexer_2 (
    .in0(left_Line_2), .in1(up_Line_2), .in2(left_Line_2), .in3(down_Line_2), .out(line_2), .sel(Way));
  Multiplexer #(.select(2), .width(32), .enable("false")) multiplexer_3 (
    .in0(left_Line_3), .in1(up_Line_3), .in2(left_Line_1), .in3(down_Line_3), .out(line_3), .sel(Way));

  // Notes on the sheet:
  //   LEFT POSITION
  //   UP POSITION
  //   DOWN POSITION
  //   OUTPUTS
endmodule

module inc5 (
  input  [4:0] in,
  output [4:0] out
);

  Adder #(.width(5)) adder_1 (.a(in), .b(5'b00001), .out(out));  // open: cin, cout
endmodule

module dec5 (
  input  [4:0] in,
  output [4:0] out
);

  Subtractor #(.width(5)) subtractor_1 (.a(in), .b(5'b00001), .out(out));  // open: bin, bout
endmodule

module driveController (
  input  [6:0] input_char,
  output [1:0] way,
  output isDrive,
  output isShot
);

  wire comparator_1_eq, comparator_2_eq, comparator_3_eq, comparator_4_eq, comparator_5_eq, comparator_6_eq,
       comparator_7_eq, comparator_8_eq, isDown, isFw, isLeft, isRight;
  wire [1:0] dw, fw, lt, rt;

  Comparator #(.width(7), .mode("unsigned")) comparator_1 (
    .a(input_char), .b(7'b1000110), .eq(comparator_1_eq));  // open: gt, lt
  Comparator #(.width(7), .mode("unsigned")) comparator_2 (
    .a(input_char), .b(7'b1110111), .eq(comparator_2_eq));  // open: gt, lt
  Comparator #(.width(7), .mode("unsigned")) comparator_3 (
    .a(input_char), .b(7'b1000100), .eq(comparator_3_eq));  // open: gt, lt
  Comparator #(.width(7), .mode("unsigned")) comparator_4 (
    .a(input_char), .b(7'b1100001), .eq(comparator_4_eq));  // open: gt, lt
  Comparator #(.width(7), .mode("unsigned")) comparator_5 (
    .a(input_char), .b(7'b1001011), .eq(comparator_5_eq));  // open: gt, lt
  Comparator #(.width(7), .mode("unsigned")) comparator_6 (
    .a(input_char), .b(7'b1110011), .eq(comparator_6_eq));  // open: gt, lt
  Comparator #(.width(7), .mode("unsigned")) comparator_7 (
    .a(input_char), .b(7'b0110010), .eq(comparator_7_eq));  // open: gt, lt
  Comparator #(.width(7), .mode("unsigned")) comparator_8 (
    .a(input_char), .b(7'b1100100), .eq(comparator_8_eq));  // open: gt, lt
  Comparator #(.width(7), .mode("unsigned")) comparator_9 (
    .a(input_char), .b(7'b0100000), .eq(isShot));  // open: gt, lt
  or or_1 (isFw, comparator_1_eq, comparator_2_eq);
  or or_2 (isLeft, comparator_3_eq, comparator_4_eq);
  or or_3 (isDown, comparator_5_eq, comparator_6_eq);
  or or_4 (isRight, comparator_7_eq, comparator_8_eq);
  assign fw = {2{isFw}} & 2'b01;  // AND_Gate and_1, 2 bits wide
  assign lt = {2{isLeft}} & 2'b00;  // AND_Gate and_2, 2 bits wide
  assign dw = {2{isDown}} & 2'b11;  // AND_Gate and_3, 2 bits wide
  assign rt = {2{isRight}} & 2'b10;  // AND_Gate and_4, 2 bits wide
  assign way = fw | lt | dw | rt;  // OR_Gate or_5, 2 bits wide
  or or_6 (isDrive, isFw, isLeft, isDown, isRight);

  // Other names for the same wires on the sheet: atck = isShot; in[6:0] = input_char

  // Notes on the sheet:
  //   FORWARD
  //   LEFT
  //   DOWN
  //   RIGHT
  //   ATTACK
endmodule

module X_cord_checker (
  input  [4:0] Y_cord,
  input  [31:0] line_1,
  input  [4:0] X_cord,
  input  [1:0] Way,
  output [4:0] req_1,
  output [4:0] X_cord_output
);

  wire and_2_out, and_3_out, and_4_out, bitfinder_1_found, comparator_1_eq, comparator_2_eq;
  wire [1:0] and_5_out, bit_extender_1_out;
  wire [4:0] dec5_1_out, dec5_2_out, dec5_3_out, dec5_4_out, inc5_1_out, inc5_2_out, inc5_3_out, inc5_4_out;
  wire [31:0] and_1_out, or_1_out, shifter_1_out, shifter_2_out, shifter_3_out;

  dec5 dec5_1 (.in(dec5_2_out), .out(dec5_1_out));
  dec5 dec5_2 (.in(X_cord), .out(dec5_2_out));
  inc5 inc5_1 (.in(inc5_2_out), .out(inc5_1_out));
  inc5 inc5_2 (.in(X_cord), .out(inc5_2_out));
  Multiplexer #(.width(5), .enable("false")) multiplexer_1 (
    .in0(dec5_1_out), .in1(inc5_1_out), .out(req_1), .sel(Way[1]));
  inc5 inc5_3 (.in(Y_cord), .out(inc5_3_out));
  dec5 dec5_3 (.in(Y_cord), .out(dec5_3_out));
  Shifter #(.width(32)) shifter_1 (.in(32'h1), .\dist (inc5_3_out), .out(shifter_1_out));
  assign or_1_out = shifter_1_out | shifter_2_out | shifter_3_out;  // OR_Gate or_1, 32 bits wide
  Shifter #(.width(32)) shifter_2 (.in(32'h1), .\dist (Y_cord), .out(shifter_2_out));
  Shifter #(.width(32)) shifter_3 (.in(32'h1), .\dist (dec5_3_out), .out(shifter_3_out));
  assign and_1_out = line_1 & or_1_out;  // AND_Gate and_1, 32 bits wide
  Comparator #(.width(5)) comparator_1 (.a(X_cord), .b(5'b11110), .eq(comparator_1_eq));  // open: gt, lt
  Comparator #(.width(5)) comparator_2 (.a(X_cord), .b(5'b00001), .eq(comparator_2_eq));  // open: gt, lt
  BitFinder #(.width(32)) bitfinder_1 (.in(and_1_out), .found(bitfinder_1_found));  // open: index
  and and_2 (and_2_out, Way[1], comparator_1_eq);
  and and_3 (and_3_out, ~bitfinder_1_found, ~and_2_out, ~Way[0], ~and_4_out);  // AND_Gate
  and and_4 (and_4_out, ~Way[1], comparator_2_eq);  // AND_Gate
  assign bit_extender_1_out = {{1{and_3_out}}, and_3_out};  // Bit_Extender bit_extender_1
  assign and_5_out = bit_extender_1_out & {1'b1, Way[1]};  // AND_Gate and_5, 2 bits wide
  Multiplexer #(.select(2), .width(5), .enable("false")) multiplexer_2 (
    .in0(X_cord), .in1(X_cord), .in2(dec5_4_out), .in3(inc5_4_out), .out(X_cord_output), .sel(and_5_out));
  dec5 dec5_4 (.in(X_cord), .out(dec5_4_out));
  inc5 inc5_4 (.in(X_cord), .out(inc5_4_out));

  // Other names for the same wires on the sheet: way_t = Way[1]; is_change = Way[0]; x[4:0] = X_cord; y[4:0] = Y_cord

  // Notes on the sheet:
  //   INPUTS
  //   NEEDFUL COLUMN
  //   CHECK COORDINATE
endmodule

module Y_cord_checker (
  input  [4:0] Y_cord,
  input  [31:0] line_1,
  input  [31:0] line_2,
  input  [31:0] line_3,
  input  [4:0] X_cord,
  input  [1:0] Way,
  output [4:0] req_1,
  output [4:0] req_2,
  output [4:0] Y_cord_output,
  output [4:0] req_3
);

  wire and_2_out, and_3_out, and_4_out, bitfinder_1_found, comparator_1_eq, comparator_2_eq;
  wire [1:0] and_5_out, bit_extender_1_out;
  wire [4:0] dec5_2_out, dec5_3_out, dec5_4_out, inc5_2_out, inc5_3_out, inc5_4_out, multiplexer_1_out;
  wire [31:0] and_1_out, or_1_out, shifter_1_out;

  dec5 dec5_1 (.in(X_cord), .out(req_1));
  inc5 inc5_1 (.in(X_cord), .out(req_3));
  inc5 inc5_2 (.in(inc5_3_out), .out(inc5_2_out));
  inc5 inc5_3 (.in(Y_cord), .out(inc5_3_out));
  dec5 dec5_2 (.in(dec5_3_out), .out(dec5_2_out));
  dec5 dec5_3 (.in(Y_cord), .out(dec5_3_out));
  Shifter #(.width(32)) shifter_1 (.in(32'h1), .\dist (multiplexer_1_out), .out(shifter_1_out));
  Multiplexer #(.width(5), .enable("false")) multiplexer_1 (
    .in0(inc5_2_out), .in1(dec5_2_out), .out(multiplexer_1_out), .sel(Way[1]));
  assign or_1_out = line_1 | line_2 | line_3;  // OR_Gate or_1, 32 bits wide
  assign and_1_out = or_1_out & shifter_1_out;  // AND_Gate and_1, 32 bits wide
  Comparator #(.width(5)) comparator_1 (.a(Y_cord), .b(5'b11110), .eq(comparator_1_eq));  // open: gt, lt
  Comparator #(.width(5)) comparator_2 (.a(Y_cord), .b(5'b00001), .eq(comparator_2_eq));  // open: gt, lt
  BitFinder #(.width(32)) bitfinder_1 (.in(and_1_out), .found(bitfinder_1_found));  // open: index
  and and_2 (and_2_out, ~Way[1], comparator_1_eq);  // AND_Gate
  and and_3 (and_3_out, ~bitfinder_1_found, ~and_2_out, Way[0], ~and_4_out);  // AND_Gate
  and and_4 (and_4_out, Way[1], comparator_2_eq);
  assign bit_extender_1_out = {{1{and_3_out}}, and_3_out};  // Bit_Extender bit_extender_1
  assign and_5_out = bit_extender_1_out & {1'b1, Way[1]};  // AND_Gate and_5, 2 bits wide
  inc5 inc5_4 (.in(Y_cord), .out(inc5_4_out));
  dec5 dec5_4 (.in(Y_cord), .out(dec5_4_out));
  Multiplexer #(.select(2), .width(5), .enable("false")) multiplexer_2 (
    .in0(Y_cord), .in1(Y_cord), .in2(inc5_4_out), .in3(dec5_4_out), .out(Y_cord_output), .sel(and_5_out));

  assign req_2 = X_cord;

  // Other names for the same wires on the sheet: way_t = Way[1]; is_change = Way[0]; x[4:0] = X_cord; y[4:0] = Y_cord

  // Notes on the sheet:
  //   INPUTS
  //   NEEDFUL COLUMNS
  //   CHECK COORDINATE
endmodule

module display_printer (
  input  [31:0] player_line_1,
  input  [31:0] player_line_2,
  input  [31:0] player_line_3,
  input  [31:0] player_bullet_line,
  input  [31:0] enemy_line_1,
  input  [31:0] enemy_line_2,
  input  [31:0] enemy_line_3,
  input  [31:0] enemy_bullet_line,
  input  [31:0] current_line,
  input  differentPlayer,
  input  clock,
  input  reset,
  input  [4:0] x_player,
  input  [4:0] x_bullet_player,
  input  [4:0] x_enemy,
  input  [4:0] x_bullet_enemy,
  output [4:0] column,
  output [31:0] picture,
  output draw_player,
  output draw_bullet_player,
  output draw_enemy,
  output draw_bullet_enemy,
  output output_reset
);

  wire and_1_out, and_3_out, bitfinder_1_found, comparator_1_eq, comparator_5_eq, comparator_6_eq, d_ff_1_qn,
       drPl, or_2_out;
  wire [3:0] counter;
  wire [4:0] dec5_1_out, dec5_2_out, dec5_3_out, dec5_4_out, inc5_1_out, inc5_2_out, inc5_3_out, inc5_4_out,
       mapColumn, multiplexer_4_out;
  wire [31:0] clear_line_1_result, clear_line_2_result, draw_line_1_result, draw_line_2_result, mapData,
       multiplexer_2_out, showplayer_1_line1, showplayer_1_line2, showplayer_1_line3, showplayer_1_line4,
       showplayer_1_line5, showplayer_1_line6, showplayer_2_line1, showplayer_2_line2, showplayer_2_line3,
       showplayer_2_line4, showplayer_2_line5, showplayer_2_line6;

  Comparator #(.width(4)) comparator_1 (.a(counter), .b(4'b0100), .eq(comparator_1_eq));  // open: gt, lt
  Comparator #(.width(4)) comparator_2 (.a(counter), .b(4'b0000), .eq(draw_bullet_player));  // open: gt, lt
  Comparator #(.width(4)) comparator_3 (.a(counter), .b(4'b1100), .eq(draw_enemy));  // open: gt, lt
  Comparator #(.width(4)) comparator_4 (.a(counter), .b(4'b1000), .eq(draw_bullet_enemy));  // open: gt, lt
  Counter #(.width(5), .max('h1f), .trigger("falling")) counter_1 (
    .Q(mapColumn), .clk(and_1_out));  // open: load, D, count, carry, clr
  and and_1 (and_1_out, clock, output_reset);
  or or_1 (output_reset, bitfinder_1_found, reset);
  BitFinder #(.width(5)) bitfinder_1 (.in(mapColumn), .found(bitfinder_1_found));  // open: index
  and and_2 (draw_player, drPl, comparator_1_eq);
  Comparator #(.width(4)) comparator_5 (.a(counter), .b(4'b0001), .eq(comparator_5_eq));  // open: gt, lt
  ROM #(.addrWidth(5), .dataWidth(32)) rom_1 (.addr(mapColumn), .data(mapData));  // open: sel
  and and_3 (and_3_out, differentPlayer, comparator_5_eq);
  clear_line clear_line_1 (
    .result(clear_line_1_result), .display_line(current_line), .character_line(player_bullet_line));
  draw_line draw_line_1 (.result(draw_line_1_result), .display_line(current_line), .character_line(player_bullet_line));
  D_Flip_Flop #(.trigger("falling")) d_ff_1 (
    .clk(clock), .D(or_2_out), .Q(drPl), .Qn(d_ff_1_qn), .en(d_ff_1_qn), .reset(comparator_6_eq));  // open: preset
  or or_2 (or_2_out, output_reset, and_3_out);
  Comparator #(.width(4)) comparator_6 (.a(counter), .b(4'b1000), .eq(comparator_6_eq));  // open: gt, lt
  Counter #(.width(4), .max('hf), .trigger("falling")) counter_2 (
    .Q(counter), .clk(clock), .clr(output_reset));  // open: load, D, count, carry
  showPlayer showplayer_1 (
    .diff(drPl), .tankLine1(player_line_1), .tankLine2(player_line_2), .tankLine3(player_line_3),
    .current(current_line), .line1(showplayer_1_line1), .line2(showplayer_1_line2),
    .line3(showplayer_1_line3), .line4(showplayer_1_line4), .line5(showplayer_1_line5),
    .line6(showplayer_1_line6));
  Multiplexer #(.width(32), .enable("false")) multiplexer_1 (
    .in0(multiplexer_2_out), .in1(mapData), .out(picture), .sel(output_reset));
  Multiplexer #(.select(4), .width(32), .enable("false")) multiplexer_2 (
    .in0(clear_line_1_result), .in1(draw_line_1_result), .in2(showplayer_1_line1), .in3(showplayer_1_line2),
    .in4(showplayer_1_line3), .in5(showplayer_1_line4), .in6(showplayer_1_line5), .in7(showplayer_1_line6),
    .in8(clear_line_2_result), .in9(draw_line_2_result), .in10(showplayer_2_line1),
    .in11(showplayer_2_line2), .in12(showplayer_2_line3), .in13(showplayer_2_line4),
    .in14(showplayer_2_line5), .in15(showplayer_2_line6), .out(multiplexer_2_out), .sel(counter));
  clear_line clear_line_2 (
    .result(clear_line_2_result), .display_line(current_line), .character_line(enemy_bullet_line));
  draw_line draw_line_2 (.result(draw_line_2_result), .display_line(current_line), .character_line(enemy_bullet_line));
  showPlayer showplayer_2 (
    .diff(1'b0), .tankLine1(enemy_line_1), .tankLine2(enemy_line_2), .tankLine3(enemy_line_3),
    .current(current_line), .line1(showplayer_2_line1), .line2(showplayer_2_line2),
    .line3(showplayer_2_line3), .line4(showplayer_2_line4), .line5(showplayer_2_line5),
    .line6(showplayer_2_line6));
  dec5 dec5_1 (.in(x_player), .out(dec5_1_out));
  inc5 inc5_1 (.in(x_player), .out(inc5_1_out));
  dec5 dec5_2 (.in(x_player), .out(dec5_2_out));
  Multiplexer #(.width(5), .enable("false")) multiplexer_3 (
    .in0(multiplexer_4_out), .in1(mapColumn), .out(column), .sel(output_reset));
  Multiplexer #(.select(4), .width(5), .enable("false")) multiplexer_4 (
    .in0(x_bullet_player), .in1(x_bullet_player), .in2(dec5_1_out), .in3(x_player), .in4(inc5_1_out),
    .in5(dec5_2_out), .in6(x_player), .in7(inc5_2_out), .in8(x_bullet_enemy), .in9(x_bullet_enemy),
    .in10(dec5_3_out), .in11(x_enemy), .in12(inc5_4_out), .in13(dec5_4_out), .in14(x_enemy),
    .in15(inc5_3_out), .out(multiplexer_4_out), .sel(counter));
  dec5 dec5_3 (.in(x_enemy), .out(dec5_3_out));
  inc5 inc5_2 (.in(x_player), .out(inc5_2_out));
  inc5 inc5_3 (.in(x_enemy), .out(inc5_3_out));
  dec5 dec5_4 (.in(x_enemy), .out(dec5_4_out));
  inc5 inc5_4 (.in(x_enemy), .out(inc5_4_out));

  // Other names for the same wires on the sheet: bpl[31:0] = player_bullet_line; clk = clock;
  //   condColumn = output_reset; cur[31:0] = current_line; ebl[31:0] = enemy_bullet_line; el1[31:0] = enemy_line_1;
  //   el2[31:0] = enemy_line_2; el3[31:0] = enemy_line_3; pl1[31:0] = player_line_1; pl2[31:0] = player_line_2;
  //   pl3[31:0] = player_line_3; plDif = differentPlayer; xbe[4:0] = x_bullet_enemy; xbp[4:0] = x_bullet_player;
  //   xe[4:0] = x_enemy; xp[4:0] = x_player

  // Notes on the sheet:
  //   INPUTS
  //   OUTPUTS SIGNAL
  //   ROM WITH MAP
  //   contents of rom_1 (hex, n*v repeats v):
  //   3800380 0 0 c6000 843c7841 c7fc7fc7 c0200007 c0200007 c0200007 c43c7847 c4200847 84200841 4200840
  //   4238840 4038040 4038040 4038040 4238840 4200840 84200841 c4200847 c43c7847 c0000807 c0000807
  //   c0000807 c7fc7fc7 843c7841 c6000 0 0 0 3800380
  //   PRINTED LINE
  //   not real
  //   <- PICTURE OBJECT
  //   CHOOSEN LINE
endmodule

module clear_line (
  input  [31:0] display_line,
  input  [31:0] character_line,
  output [31:0] result
);

  assign result = display_line & ~character_line;  // AND_Gate and_1, 32 bits wide
endmodule

module draw_line (
  input  [31:0] display_line,
  input  [31:0] character_line,
  output [31:0] result
);

  assign result = display_line | character_line;  // OR_Gate or_1, 32 bits wide
endmodule

module showPlayer (
  input  diff,
  input  [31:0] tankLine1,
  input  [31:0] tankLine2,
  input  [31:0] tankLine3,
  input  [31:0] current,
  output [31:0] line1,
  output [31:0] line2,
  output [31:0] line3,
  output [31:0] line4,
  output [31:0] line5,
  output [31:0] line6
);

  wire [31:0] clear_line_1_result, clear_line_2_result, clear_line_3_result, draw_line_1_result,
       draw_line_2_result, draw_line_3_result;

  Multiplexer #(.width(32), .enable("false")) multiplexer_1 (
    .in0(current), .in1(clear_line_1_result), .out(line1), .sel(diff));
  clear_line clear_line_1 (.result(clear_line_1_result), .display_line(current), .character_line(tankLine1));
  Multiplexer #(.width(32), .enable("false")) multiplexer_2 (
    .in0(current), .in1(clear_line_2_result), .out(line2), .sel(diff));
  clear_line clear_line_2 (.result(clear_line_2_result), .display_line(current), .character_line(tankLine2));
  Multiplexer #(.width(32), .enable("false")) multiplexer_3 (
    .in0(current), .in1(clear_line_3_result), .out(line3), .sel(diff));
  clear_line clear_line_3 (.result(clear_line_3_result), .display_line(current), .character_line(tankLine3));
  Multiplexer #(.width(32), .enable("false")) multiplexer_4 (
    .in0(current), .in1(draw_line_1_result), .out(line4), .sel(diff));
  draw_line draw_line_1 (.result(draw_line_1_result), .display_line(current), .character_line(tankLine1));
  Multiplexer #(.width(32), .enable("false")) multiplexer_5 (
    .in0(current), .in1(draw_line_2_result), .out(line5), .sel(diff));
  draw_line draw_line_2 (.result(draw_line_2_result), .display_line(current), .character_line(tankLine2));
  Multiplexer #(.width(32), .enable("false")) multiplexer_6 (
    .in0(current), .in1(draw_line_3_result), .out(line6), .sel(diff));
  draw_line draw_line_3 (.result(draw_line_3_result), .display_line(current), .character_line(tankLine3));

  // Other names for the same wires on the sheet: cur[31:0] = current; t1[31:0] = tankLine1; t2[31:0] = tankLine2;
  //   t3[31:0] = tankLine3

  // Notes on the sheet:
  //   INPUTS
  //   <- PICTURE OBJECT
endmodule

module dispayStateGame (
  input  clock,
  input  wEnemy,
  input  wPlayer,
  input  start,
  output [30:0] out_5,
  output [30:0] out_6,
  output [30:0] out_7,
  output [30:0] out_8,
  output [30:0] out_9,
  output [30:0] out_10,
  output [30:0] out_11
);

  wire and_1_out, ch0, ch1, ch2, ch3, ch4, ch5, ch6, comparator_1_gt, comparator_1_lt, comparator_2_gt,
       comparator_2_lt, or_1_out;
  wire [1:0] typeTextLast;
  wire [2:0] counter;
  wire [30:0] line0, line1, line2, line3, line4, line5, line6, multiplexer_1_out, rom_1_data, rom_2_data,
       rom_3_data, rom_4_data;

  Demultiplexer #(.select(3), .enable("false")) demultiplexer_1 (
    .out0(ch0), .out1(ch1), .out2(ch2), .out3(ch3), .out4(ch4), .out5(ch5), .out6(ch6), .in(1'b1),
    .sel(counter));  // open: out7
  Register #(.width(2), .trigger("falling")) register_1 (
    .D({wPlayer, wEnemy}), .Q(typeTextLast), .clk(clock));  // open: en, clr
  ROM #(.addrWidth(3), .dataWidth(31)) rom_1 (.addr(counter), .data(rom_1_data));  // open: sel
  ROM #(.addrWidth(3), .dataWidth(31)) rom_2 (.addr(counter), .data(rom_2_data));  // open: sel
  ROM #(.addrWidth(3), .dataWidth(31)) rom_3 (.addr(counter), .data(rom_3_data));  // open: sel
  ROM #(.addrWidth(3), .dataWidth(31)) rom_4 (.addr(counter), .data(rom_4_data));  // open: sel
  Multiplexer #(.select(2), .width(31), .enable("false")) multiplexer_1 (
    .in0(rom_1_data), .in1(rom_2_data), .in2(rom_3_data), .in3(rom_4_data), .out(multiplexer_1_out),
    .sel({wPlayer, wEnemy}));
  Demultiplexer #(.select(3), .width(31), .enable("false")) demultiplexer_2 (
    .out0(line0), .out1(line1), .out2(line2), .out3(line3), .out4(line4), .out5(line5), .out6(line6),
    .in(multiplexer_1_out), .sel(counter));  // open: out7
  Counter #(.width(3), .max('h6), .trigger("falling")) counter_1 (
    .Q(counter), .clk(and_1_out));  // open: load, D, count, carry, clr
  and and_1 (and_1_out, clock, or_1_out);
  or or_1 (or_1_out, comparator_1_gt, comparator_1_lt, start, comparator_2_gt, comparator_2_lt);
  Comparator #(.width(2)) comparator_1 (
    .a(typeTextLast), .b({wPlayer, wEnemy}), .gt(comparator_1_gt), .lt(comparator_1_lt));  // open: eq
  Comparator #(.width(3)) comparator_2 (
    .a(3'b000), .b(counter), .gt(comparator_2_gt), .lt(comparator_2_lt));  // open: eq
  Register #(.width(31), .trigger("falling")) register_2 (.D(line0), .en(ch0), .Q(out_5), .clk(clock));  // open: clr
  Register #(.width(31), .trigger("falling")) register_3 (.D(line1), .en(ch1), .Q(out_6), .clk(clock));  // open: clr
  Register #(.width(31), .trigger("falling")) register_4 (.D(line2), .en(ch2), .Q(out_7), .clk(clock));  // open: clr
  Register #(.width(31), .trigger("falling")) register_5 (.D(line3), .en(ch3), .Q(out_8), .clk(clock));  // open: clr
  Register #(.width(31), .trigger("falling")) register_6 (.D(line4), .en(ch4), .Q(out_9), .clk(clock));  // open: clr
  Register #(.width(31), .trigger("falling")) register_7 (.D(line5), .en(ch5), .Q(out_10), .clk(clock));  // open: clr
  Register #(.width(31), .trigger("falling")) register_8 (.D(line6), .en(ch6), .Q(out_11), .clk(clock));  // open: clr

  // Other names for the same wires on the sheet: clk = clock; typeText[1:0] = {wPlayer, wEnemy}

  // Notes on the sheet:
  //   INPUTS
  //   CHOOSEN LINE
  //   contents of rom_1 (hex, n*v repeats v):
  //   742500 545500 545500 645700 447200 455200 475200
  //   contents of rom_2 (hex, n*v repeats v):
  //   57504777 55504554 55504544 75504577 25504514 25505554 27707777
  //   contents of rom_3 (hex, n*v repeats v):
  //   2ba855d2 2aa8549a 2aa85496 3aa85492 12a85492 12a85492 13b829d2
  //   contents of rom_4 (hex, n*v repeats v):
  //   ce4a80 aaaa80 aaaa80 acaa80 aaea80 aaaa80 caa500
  //   ROM WITH TEXT
  //   CLOCK LIMITER
  //   OUTPUT LINES
endmodule

module bulletController (
  input  reset,
  input  stateUpdate,
  input  clock,
  input  shot,
  input  [4:0] xStart,
  input  [4:0] yStart,
  input  [1:0] way,
  input  [4:0] xEnemy,
  input  [4:0] yEnemy,
  output [31:0] outputLine,
  output [4:0] xOutput,
  output defeatTartget
);

  wire and_3_out, bitfinder_1_found, comparator_1_eq, comparator_2_eq, comparator_3_eq, comparator_4_eq,
       comparator_5_eq, comparator_5_lt, comparator_6_eq, comparator_6_lt, multiplexer_5_out, not_1_out,
       not_2_out, not_3_out, not_4_out, or_1_out, or_2_out, or_3_out, or_4_out, or_5_out, state;
  wire [1:0] counter, multiplexer_3_out, way_t;
  wire [4:0] dec5_1_out, dec5_2_out, inc5_1_out, inc5_2_out, minmaxmodule_1_res, minmaxmodule_2_res,
       minmaxmodule_3_res, minmaxmodule_4_res, multiplexer_1_out, multiplexer_2_out, resX, resY,
       subtractor_1_out, subtractor_2_out, xB, yB;
  wire [31:0] and_1_out, and_4_out, bit_extender_1_out, rom_1_data, shifter_1_out, shifter_2_out;

  Multiplexer #(.width(5), .enable("false")) multiplexer_1 (
    .in0(xStart), .in1(resX), .out(multiplexer_1_out), .sel(state));
  Multiplexer #(.width(5), .enable("false")) multiplexer_2 (
    .in0(yStart), .in1(resY), .out(multiplexer_2_out), .sel(state));
  Multiplexer #(.width(2), .enable("false")) multiplexer_3 (
    .in0(way), .in1(way_t), .out(multiplexer_3_out), .sel(state));
  Register #(.width(5), .trigger("falling")) xBulletLast (
    .D(xB), .Q(xOutput), .clk(stateUpdate), .clr(reset));  // open: en
  Register #(.width(5), .trigger("falling")) xBullet (.D(multiplexer_1_out), .Q(xB), .clk(clock));  // open: en, clr
  Register #(.width(5), .trigger("falling")) yBullet (.D(multiplexer_2_out), .Q(yB), .clk(clock));  // open: en, clr
  Register #(.width(2), .trigger("falling")) u_way (.D(multiplexer_3_out), .Q(way_t), .clk(clock));  // open: en, clr
  inc5 inc5_1 (.in(yB), .out(inc5_1_out));
  dec5 dec5_1 (.in(yB), .out(dec5_1_out));
  Multiplexer #(.select(2), .width(5), .enable("false")) multiplexer_4 (
    .in0(yB), .in1(inc5_1_out), .in2(yB), .in3(dec5_1_out), .out(resY), .sel(way_t));
  ROM #(.addrWidth(5), .dataWidth(32)) rom_1 (.addr(resX), .data(rom_1_data));  // open: sel
  Shifter #(.width(32)) shifter_1 (.in(32'h1), .\dist (resY), .out(shifter_1_out));
  Comparator #(.width(5)) comparator_1 (.a({5{1'b0}}), .b(xB), .eq(comparator_1_eq));  // open: gt, lt
  Comparator #(.width(5)) comparator_2 (.a({5{1'b1}}), .b(yB), .eq(comparator_2_eq));  // open: gt, lt
  Comparator #(.width(5)) comparator_3 (.a({5{1'b1}}), .b(xB), .eq(comparator_3_eq));  // open: gt, lt
  Comparator #(.width(5)) comparator_4 (.a({5{1'b0}}), .b(yB), .eq(comparator_4_eq));  // open: gt, lt
  minMaxModule minmaxmodule_1 (.Max(1'b1), .num1(xB), .num2(xEnemy), .res(minmaxmodule_1_res));
  Subtractor #(.width(5)) subtractor_1 (
    .a(minmaxmodule_1_res), .b(minmaxmodule_2_res), .out(subtractor_1_out));  // open: bin, bout
  minMaxModule minmaxmodule_2 (.num1(xB), .num2(xEnemy), .res(minmaxmodule_2_res));  // open: Max
  minMaxModule minmaxmodule_3 (.Max(1'b1), .num1(yB), .num2(yEnemy), .res(minmaxmodule_3_res));
  Subtractor #(.width(5)) subtractor_2 (
    .a(minmaxmodule_3_res), .b(minmaxmodule_4_res), .out(subtractor_2_out));  // open: bin, bout
  minMaxModule minmaxmodule_4 (.num1(yB), .num2(yEnemy), .res(minmaxmodule_4_res));  // open: Max
  BitFinder #(.width(32)) bitfinder_1 (.in(and_1_out), .found(bitfinder_1_found));  // open: index
  assign and_1_out = rom_1_data & shifter_1_out;  // AND_Gate and_1, 32 bits wide
  not not_1 (not_1_out, comparator_1_eq);
  not not_2 (not_2_out, comparator_2_eq);
  Multiplexer #(.select(2), .enable("false")) multiplexer_5 (
    .in0(not_1_out), .in1(not_2_out), .in2(not_3_out), .in3(not_4_out), .out(multiplexer_5_out), .sel(way_t));
  not not_3 (not_3_out, comparator_3_eq);
  not not_4 (not_4_out, comparator_4_eq);
  Comparator #(.width(5), .mode("unsigned")) comparator_5 (
    .a(subtractor_1_out), .b(5'b00001), .eq(comparator_5_eq), .lt(comparator_5_lt));  // open: gt
  Comparator #(.width(5), .mode("unsigned")) comparator_6 (
    .a(subtractor_2_out), .b(5'b00001), .eq(comparator_6_eq), .lt(comparator_6_lt));  // open: gt
  D_Flip_Flop currentState (.clk(shot), .D(shot), .Q(state), .reset(or_1_out));  // open: Qn, preset, en
  or or_1 (or_1_out, or_2_out, reset);
  or or_2 (or_2_out, bitfinder_1_found, ~multiplexer_5_out);  // OR_Gate
  or or_3 (or_3_out, comparator_5_eq, comparator_5_lt);
  and and_2 (defeatTartget, or_3_out, state, or_4_out);
  or or_4 (or_4_out, comparator_6_eq, comparator_6_lt);
  Multiplexer #(.select(2), .width(5), .enable("false")) multiplexer_6 (
    .in0(dec5_2_out), .in1(xB), .in2(inc5_2_out), .in3(xB), .out(resX), .sel(way_t));
  inc5 inc5_2 (.in(xB), .out(inc5_2_out));
  dec5 dec5_2 (.in(xB), .out(dec5_2_out));
  Shifter #(.width(32)) shifter_2 (.in(32'h1), .\dist (yB), .out(shifter_2_out));
  assign bit_extender_1_out = {{31{and_3_out}}, and_3_out};  // Bit_Extender bit_extender_1
  and and_3 (and_3_out, state, counter[0], counter[1]);
  Counter #(.width(2), .max('h3), .ongoal("stay")) counter_1 (
    .Q(counter), .clk(clock), .clr(or_5_out));  // open: load, D, count, carry
  or or_5 (or_5_out, reset, ~state);  // OR_Gate
  assign and_4_out = shifter_2_out & bit_extender_1_out;  // AND_Gate and_4, 32 bits wide
  Register #(.width(32), .trigger("falling")) register_1 (
    .D(and_4_out), .Q(outputLine), .clk(stateUpdate), .clr(reset));  // open: en

  // Other names for the same wires on the sheet: clk = clock; stUp = stateUpdate

  // Notes on the sheet:
  //   INPUTS
  //   X COORDINATE BULLET
  //   Y COORDINATE BULLET
  //   DIRECT BULLET
  //   X LAST COORDINATE BULLET
  //   contents of rom_1 (hex, n*v repeats v):
  //   3800380 0 0 c6000 843c7841 c7fc7fc7 c0200007 c0200007 c0200007 c43c7847 c4200847 84200841 4200840
  //   4238840 4038040 4038040 4038040 4238840 4200840 84200841 c4200847 c43c7847 c0000807 c0000807
  //   c0000807 c7fc7fc7 843c7841 c6000 0 0 0 3800380
  //   WIN CHECKING
  //   CHECKING STATUS
  //   CHOSEN COORDINATE
  //   OUTPUT LINE
  //   UPDATE LIMITER
endmodule

module minMaxModule (
  input  Max,
  input  [4:0] num1,
  input  [4:0] num2,
  output [4:0] res
);

  wire comparator_1_gt, xor_1_out;

  Comparator #(.width(5), .mode("unsigned")) comparator_1 (.a(num1), .b(num2), .gt(comparator_1_gt));  // open: eq, lt
  xor xor_1 (xor_1_out, comparator_1_gt, Max);
  Multiplexer #(.width(5), .enable("false")) multiplexer_1 (.in0(num1), .in1(num2), .out(res), .sel(xor_1_out));

  // Notes on the sheet:
  //   Max: pull=down
endmodule

module tankObjectEnemy (
  input  clock,
  input  stateUpdate,
  input  Reset,
  input  [4:0] xPlayer,
  input  [4:0] yPlayer,
  input  [1:0] way,
  input  isDrive,
  input  isShot,
  output [31:0] out_9,
  output [31:0] out_10,
  output [31:0] out_11,
  output [4:0] xCur,
  output [4:0] yCur,
  output [1:0] wayCur,
  output [4:0] X_output,
  output differentCord,
  output [4:0] xCordPlayer,
  output isShot_2,
  output [4:0] yCordPlayer
);

  wire comparator_1_gt, comparator_1_lt, comparator_2_gt, comparator_2_lt, comparator_3_gt, comparator_3_lt,
       comparator_4_gt, comparator_4_lt, comparator_5_gt, comparator_5_lt, drive, or_2_out, or_3_out,
       or_4_out, or_6_out, or_7_out;
  wire [1:0] DirectionTank_q, dirTank1, multiplexer_3_out;
  wire [4:0] dec5_1_out, dec5_2_out, inc5_1_out, inc5_2_out, multiplexer_1_out, multiplexer_2_out,
       multiplexer_5_out, multiplexer_6_out;
  wire [5:5] subtractor_1_out;
  wire [31:0] pctIn1, pctIn2, pctIn3;

  or or_1 (drive, isDrive, Reset);
  Comparator #(.width(5)) comparator_1 (
    .a(xCur), .b(X_output), .gt(comparator_1_gt), .lt(comparator_1_lt));  // open: eq
  Comparator #(.width(2)) comparator_2 (
    .a(dirTank1), .b(wayCur), .gt(comparator_2_gt), .lt(comparator_2_lt));  // open: eq
  Comparator #(.width(32)) comparator_3 (
    .a(pctIn1), .b(out_9), .gt(comparator_3_gt), .lt(comparator_3_lt));  // open: eq
  Comparator #(.width(32)) comparator_4 (
    .a(pctIn2), .b(out_10), .gt(comparator_4_gt), .lt(comparator_4_lt));  // open: eq
  Comparator #(.width(32)) comparator_5 (
    .a(pctIn3), .b(out_11), .gt(comparator_5_gt), .lt(comparator_5_lt));  // open: eq
  or or_2 (or_2_out, comparator_1_gt, comparator_1_lt);
  or or_3 (or_3_out, comparator_2_gt, comparator_2_lt);
  or or_4 (or_4_out, comparator_3_gt, comparator_3_lt);
  or or_5 (differentCord, or_2_out, or_3_out, or_4_out, or_6_out, or_7_out);
  or or_6 (or_6_out, comparator_4_gt, comparator_4_lt);
  or or_7 (or_7_out, comparator_5_gt, comparator_5_lt);
  dec5 dec5_1 (.in(xCur), .out(dec5_1_out));
  inc5 inc5_1 (.in(xCur), .out(inc5_1_out));
  Register #(.width(2), .trigger("falling")) DirectionTank1 (
    .D(wayCur), .Q(dirTank1), .clk(stateUpdate), .clr(Reset));  // open: en
  Multiplexer #(.select(2), .width(5), .enable("false")) multiplexer_1 (
    .in0(dec5_1_out), .in1(xCur), .in2(inc5_1_out), .in3(xCur), .out(multiplexer_1_out), .sel(wayCur));
  Multiplexer #(.width(5), .enable("false")) multiplexer_2 (
    .in0(multiplexer_1_out), .in1({5{1'b1}}), .out(multiplexer_2_out), .sel(Reset));
  Register #(.width(5), .trigger("falling")) xTank (
    .D(multiplexer_2_out), .en(drive), .Q(xCur), .clk(clock));  // open: clr
  Register #(.width(5), .trigger("falling")) xTank1 (
    .D(xCur), .Q(X_output), .clk(stateUpdate), .clr(Reset));  // open: en
  Register #(.width(2), .trigger("falling")) DirectionTank (
    .D(multiplexer_3_out), .en(drive), .Q(DirectionTank_q), .clk(clock));  // open: clr
  Multiplexer #(.width(2), .enable("false")) multiplexer_3 (
    .in0(way), .in1(2'b11), .out(multiplexer_3_out), .sel(Reset));
  inc5 inc5_2 (.in(yCur), .out(inc5_2_out));
  dec5 dec5_2 (.in(yCur), .out(dec5_2_out));
  Multiplexer #(.width(2), .enable("false")) multiplexer_4 (
    .in0(DirectionTank_q), .in1(way), .out(wayCur), .sel(drive));
  Multiplexer #(.select(2), .width(5), .enable("false")) multiplexer_5 (
    .in0(yCur), .in1(inc5_2_out), .in2(yCur), .in3(dec5_2_out), .out(multiplexer_5_out), .sel(wayCur));
  Multiplexer #(.width(5), .enable("false")) multiplexer_6 (
    .in0(multiplexer_5_out), .in1({5{1'b1}}), .out(multiplexer_6_out), .sel(Reset));
  Register #(.width(5), .trigger("falling")) yTank (
    .D(multiplexer_6_out), .en(drive), .Q(yCur), .clk(clock));  // open: clr
  drawTank drawtank_1 (.Y(yCur), .Way(wayCur), .line_1(pctIn1), .line_2(pctIn2), .line_3(pctIn3));
  Subtractor #(.width(6)) subtractor_1 (
    .a(6'b011111), .b({1'b0, yPlayer}), .out({subtractor_1_out[5], yCordPlayer}));  // open: bin, bout
  Register #(.width(32), .trigger("falling")) register_1 (
    .D(pctIn1), .Q(out_9), .clk(stateUpdate), .clr(Reset));  // open: en
  Register #(.width(32), .trigger("falling")) register_2 (
    .D(pctIn2), .Q(out_10), .clk(stateUpdate), .clr(Reset));  // open: en
  Register #(.width(32), .trigger("falling")) register_3 (
    .D(pctIn3), .Q(out_11), .clk(stateUpdate), .clr(Reset));  // open: en

  assign isShot_2 = isShot;
  assign xCordPlayer = xPlayer;

  // Other names for the same wires on the sheet: clk = clock; dirTank[1:0] = wayCur; pctOut1[31:0] = out_9;
  //   pctOut2[31:0] = out_10; pctOut3[31:0] = out_11; state_up = stateUpdate; x_cord_tank[4:0] = xCur;
  //   x_cord_tank1[4:0] = X_output; y_cord_tank[4:0] = yCur

  // Notes on the sheet:
  //   INPUTS
  //   IS DIFFERENT COORDINAT OR ROTATE TANK
  //   LAST DIRECTION TANK
  //   X COORDINATE TANK
  //   LAST X COORDINATE TANK
  //   INPUT DATA FROM PROCESSOR
  //   DIRECTION TANK
  //   Y COORDINATE TANK
  //   OUTPUTS
  //   INPUT DATA FOR PROCESSOR
  //   IMAGE TANK
endmodule
